# Fritzing sketch harp (saved by Fritzing 0.9.3b)

parts:
  Part1 = Arduino Uno (Rev3)
  R1 = Photocell (LDR) [package=THT]
  R2 = Photocell (LDR) [package=THT]
  R3 = Photocell (LDR) [package=THT]
  R4 = Photocell (LDR) [package=THT]
  R5 = Photocell (LDR) [package=THT]
  R6 = Photocell (LDR) [package=THT]
  R8 = Resistor [tolerance=±5% resistance=220 package=THT]
  R9 = Resistor [tolerance=±5% resistance=220 package=THT]
  R10 = Resistor [tolerance=±5% resistance=220 package=THT]
  R11 = Resistor [tolerance=±5% resistance=220 package=THT]
  R12 = Resistor [tolerance=±5% resistance=220 package=THT]
  R14 = Resistor [tolerance=±5% resistance=220 package=THT]
  LED1 = LED - 5mm [color="Red (633nm)" package="5 mm [THT]"]
  LED2 = LED - 5mm [color="Red (633nm)" package="5 mm [THT]"]
  LED3 = LED - 5mm [color="Red (633nm)" package="5 mm [THT]"]
  LED4 = LED - 5mm [color="Red (633nm)" package="5 mm [THT]"]
  LED5 = LED - 5mm [color="Red (633nm)" package="5 mm [THT]"]
  LED6 = LED - 5mm [color="Red (633nm)" package="5 mm [THT]"]

nets:
  N1: Part1.GND, R8.Pin_0, R9.Pin_0, R10.Pin_0, R11.Pin_0, R12.Pin_0, R14.Pin_0, LED1.cathode, LED2.cathode, LED3.cathode, LED4.cathode, LED5.cathode, LED6.cathode
  N2: Part1.D2, R1.pin_0, R8.Pin_1
  N3: Part1.D3_PWM, R2.pin_0, R11.Pin_1
  N4: Part1.D4, R3.pin_0, R10.Pin_1
  N5: Part1.D5_PWM, R4.pin_0, R9.Pin_1
  N6: Part1.D6_PWM, R5.pin_0, R12.Pin_1
  N7: Part1.D7, R6.pin_0, R14.Pin_1
  N8: Part1.3V3, R1.pin_1, R2.pin_1, R3.pin_1, R4.pin_1, R5.pin_1, R6.pin_1
  N9: Part1.5V, LED1.anode, LED2.anode, LED3.anode, LED4.anode, LED5.anode, LED6.anode
